// Logisim project cpu.circ as structural Verilog: 16 circuits, main circuit main
// CPU
module main (
  input  [31:0] RS_READ_VALUE,
  input  [31:0] RI_READ_VALUE,
  input  [31:0] RD_READ_VALUE,
  input  [31:0] JC_READ_VALUE,
  input  [31:0] INSTRUCTION,
  input  CLOCK,
  output [4:0] RS,
  output [4:0] RI,
  output [4:0] RD,
  output [31:0] RD_WRITE_VALUE,
  output RD_WRITE_ENABLE,
  output [23:0] FETCH_ADDRESS
);

  wire GO_MEM, I, J_SELECT, JAL, MEM_WRITE, WORD_MODE;
  wire [2:0] JC;
  wire [3:0] OP;
  wire [4:0] RD_t;
  wire [16:0] IMM;
  wire [23:0] ADDR, JUMP_ADDR, ra;
  wire [31:0] ALU_RESULT, MEM_RESULT, multiplexer_2_out, multiplexer_4_out;
  wire [31:17] IMM_SIGN_EXT;

  Multiplexer #(.width(5)) multiplexer_1 (.in0(RD_t), .in1(5'b00110), .out(RD), .sel(JAL));  // open: en
  u_DECODE u_decode_1 (
    .Instruction(INSTRUCTION), .RD(RD_t), .RS(RS), .IMM(IMM), .RI(RI), .ADDR(ADDR), .JC(JC), .I(I), .OP(OP));
  u_PC u_pc_1 (.PC_1(ra), .J_ADDR(JUMP_ADDR), .ADDR_1(ra), .PC_SELECT(J_SELECT), .CLK(CLOCK), .ADDR(FETCH_ADDRESS));
  Multiplexer #(.width(32)) multiplexer_2 (
    .in0(RI_READ_VALUE), .in1({IMM_SIGN_EXT, IMM}), .out(multiplexer_2_out), .sel(I));  // open: en
  u_CTRL u_ctrl_1 (
    .OP(OP), .JC(JC), .JC_VALUE(JC_READ_VALUE), .J_SELECT(J_SELECT), .JAL(JAL),
    .RD_WRITING_ENABLE(RD_WRITE_ENABLE), .WORD_MODE(WORD_MODE), .GO_MEM(GO_MEM), .MEM_WRITE(MEM_WRITE));
  u_ALU u_alu_1 (.ALU_X(RS_READ_VALUE), .ALU_Y(multiplexer_2_out), .ALU_RESULT(ALU_RESULT), .ALU_CONTROL(OP));
  u_MEM u_mem_1 (
    .ADDRESS(ALU_RESULT[24:0]), .WORD_MODE(WORD_MODE), .MEM_WRITE(MEM_WRITE), .DATA_IN(RD_READ_VALUE),
    .CLOCK(CLOCK), .DATA_OUT(MEM_RESULT));
  Multiplexer #(.width(15)) multiplexer_3 (
    .in0({15{1'b0}}), .in1({15{1'b1}}), .out(IMM_SIGN_EXT), .sel(IMM[16]));  // open: en
  Multiplexer #(.width(32)) multiplexer_4 (
    .in0(ALU_RESULT), .in1(MEM_RESULT), .out(multiplexer_4_out), .sel(GO_MEM));  // open: en
  Multiplexer #(.width(32)) multiplexer_5 (
    .in0(multiplexer_4_out), .in1({{8{1'b0}}, ra}), .out(RD_WRITE_VALUE), .sel(JAL));  // open: en
  Multiplexer #(.width(24)) multiplexer_6 (
    .in0(RI_READ_VALUE[23:0]), .in1(ADDR), .out(JUMP_ADDR), .sel(I));  // open: en

  // Other names for the same wires on the sheet: CLK = CLOCK; IMM_SIGN_EXT[16:0] = IMM;
  //   JC_VALUE[31:0] = JC_READ_VALUE; RD_ENABLE = RD_WRITE_ENABLE; RD_VALUE[31:0] = RD_READ_VALUE;
  //   RD_W_V[31:0] = RD_WRITE_VALUE; RI_VALUE[31:0] = RI_READ_VALUE; RS_VALUE[31:0] = RS_READ_VALUE

  // Notes on the sheet:
  //   Feel free to use these ALU/MEM components, or delete them!
endmodule

module u_ALU (
  input  [31:0] ALU_X,
  input  [31:0] ALU_Y,
  input  [3:0] ALU_CONTROL,
  output [31:0] ALU_RESULT
);

  wire [31:0] adder_1_out, adder_2_out, and_1_out, multiplier_1_out, or_1_out, shifter_1_out,
       subtractor_1_out, u_div_1_output, u_rev_1_output, u_sl_1_sl_output, xor_1_out;

  u_SL u_sl_1 (.RS(ALU_X), .RI_MM_0_4(ALU_Y[4:0]), .SL_OUTPUT(u_sl_1_sl_output));
  Shifter #(.width(32), .shift("ar")) shifter_1 (.in(ALU_X), .\dist (ALU_Y[4:0]), .out(shifter_1_out));
  assign and_1_out = ALU_X & ALU_Y;  // AND_Gate and_1, 32 bits wide
  assign or_1_out = ALU_X | ALU_Y;  // OR_Gate or_1, 32 bits wide
  u_REV u_rev_1 (.INPUT(ALU_X), .REVERSE_AMOUNT(ALU_Y[4:0]), .OUTPUT(u_rev_1_output));
  assign xor_1_out = ALU_X ^ ALU_Y;  // XOR_Gate xor_1, 32 bits wide
  Adder #(.width(32)) adder_1 (.a(ALU_X), .b(ALU_Y), .out(adder_1_out));  // open: cin, cout
  Subtractor #(.width(32)) subtractor_1 (.a(ALU_X), .b(ALU_Y), .out(subtractor_1_out));  // open: bin, bout
  Multiplier #(.width(32)) multiplier_1 (.a(ALU_X), .b(ALU_Y), .out(multiplier_1_out));  // open: cin, cout
  u_DIV u_div_1 (.RS(ALU_X), .RI_IMM(ALU_Y), .OUTPUT(u_div_1_output));
  Adder #(.width(32)) adder_2 (.a(ALU_X), .b(ALU_Y), .out(adder_2_out));  // open: cin, cout
  Multiplexer #(.select(4), .width(32)) multiplexer_1 (
    .in0(u_sl_1_sl_output), .in1(shifter_1_out), .in2(and_1_out), .in3(or_1_out), .in4(u_rev_1_output),
    .in5(xor_1_out), .in6(adder_1_out), .in7(subtractor_1_out), .in8(multiplier_1_out), .in9(u_div_1_output),
    .in10(adder_2_out), .in11(adder_2_out), .in12(adder_2_out), .in13(adder_2_out),
    .in14({ALU_Y[16:0], ALU_X[14:0]}), .in15({32{1'b0}}), .out(ALU_RESULT), .sel(ALU_CONTROL));  // open: en
  // Probe on ALU_CONTROL
  // Probe on ALU_RESULT

  // Other names for the same wires on the sheet: RS[31:0] = ALU_X; RS_0 = ALU_X[0]; OUT[31:0] = ALU_RESULT;
  //   RI_IMM[31:0] = ALU_Y; RI_IMM_0_4[4:0] = ALU_Y[4:0]; RS_31 = ALU_X[31]

  // Notes on the sheet:
  //   Feel free to use this component, or not, however you want!
endmodule

// Data Memory
module u_MEM (
  input  [24:0] ADDRESS,
  input  WORD_MODE,
  input  MEM_WRITE,
  input  [31:0] DATA_IN,
  input  CLOCK,
  output [31:0] DATA_OUT
);

  wire and_1_out, and_2_out, demultiplexer_1_out0, demultiplexer_1_out1, not_1_out, or_1_out, or_2_out, REM;
  wire [15:0] A, B, multiplexer_1_out, multiplexer_2_out, multiplexer_3_out, multiplexer_4_out;
  wire [23:0] adder_1_out;
  wire [24:0] divider_1_out;
  wire [24:1] divider_1_rem;

  Divider #(.width(25)) divider_1 (
    .a(ADDRESS), .b(25'h2), .out(divider_1_out), .rem({divider_1_rem, REM}));  // open: upper
  Demultiplexer demultiplexer_1 (
    .out0(demultiplexer_1_out0), .out1(demultiplexer_1_out1), .in(1'b1), .sel(REM));  // open: en
  Adder #(.width(24)) adder_1 (
    .a(divider_1_out[23:0]), .b({divider_1_rem[23:1], REM}), .out(adder_1_out));  // open: cin, cout
  Multiplexer #(.width(16)) multiplexer_1 (
    .in0(DATA_IN[15:0]), .in1(DATA_IN[31:16]), .out(multiplexer_1_out), .sel(REM));  // open: en
  or or_1 (or_1_out, demultiplexer_1_out0, WORD_MODE);
  and and_1 (and_1_out, MEM_WRITE, or_1_out);
  RAM #(.addrWidth(24), .dataWidth(16), .bus("separate")) ram_1 (
    .addr(adder_1_out), .din(multiplexer_1_out), .data(A), .str(and_1_out), .clk(CLOCK), .ld(1'b1));  // open: sel, clr
  not not_1 (not_1_out, REM);
  Multiplexer #(.width(16)) multiplexer_2 (
    .in0(DATA_IN[15:0]), .in1(DATA_IN[31:16]), .out(multiplexer_2_out), .sel(not_1_out));  // open: en
  or or_2 (or_2_out, demultiplexer_1_out1, WORD_MODE);
  and and_2 (and_2_out, MEM_WRITE, or_2_out);
  RAM #(.addrWidth(24), .dataWidth(16), .bus("separate")) ram_2 (
    .addr(divider_1_out[23:0]), .din(multiplexer_2_out), .data(B), .str(and_2_out), .clk(CLOCK), .ld(1'b1));  // open: sel, clr
  Multiplexer #(.width(16)) multiplexer_3 (
    .in0({16{1'b0}}), .in1({16{1'b1}}), .out(multiplexer_3_out), .sel(A[15]));  // open: en
  Multiplexer #(.width(16)) multiplexer_4 (
    .in0({16{1'b0}}), .in1({16{1'b1}}), .out(multiplexer_4_out), .sel(B[15]));  // open: en
  Multiplexer #(.select(2), .width(32)) multiplexer_5 (
    .in0({multiplexer_3_out, A}), .in1({multiplexer_4_out, B}), .in2({B, A}), .in3({A, B}), .out(DATA_OUT),
    .sel({WORD_MODE, REM}));  // open: en

  // Other names for the same wires on the sheet: CLK = CLOCK; LOWER[15:0] = DATA_IN[15:0];
  //   HIGHER[15:0] = DATA_IN[31:16]
endmodule

module u_REV (
  input  [31:0] INPUT,
  input  [4:0] REVERSE_AMOUNT,
  output [31:0] OUTPUT
);

  wire [31:0] multiplexer_1_out, multiplexer_2_out, multiplexer_3_out, multiplexer_4_out, REV0_output,
       REV1_output, REV_2_output, REV_3_output, REV_4_output;

  Multiplexer #(.width(32)) multiplexer_1 (
    .in0(INPUT), .in1(REV0_output), .out(multiplexer_1_out), .sel(REVERSE_AMOUNT[0]));  // open: en
  u_REV_0 REV0 (.INPUT(INPUT), .OUTPUT(REV0_output));
  Multiplexer #(.width(32)) multiplexer_2 (
    .in0(multiplexer_1_out), .in1(REV1_output), .out(multiplexer_2_out), .sel(REVERSE_AMOUNT[1]));  // open: en
  u_REV_1 REV1 (.INPUT(multiplexer_1_out), .OUTPUT(REV1_output));
  Multiplexer #(.width(32)) multiplexer_3 (
    .in0(multiplexer_2_out), .in1(REV_2_output), .out(multiplexer_3_out), .sel(REVERSE_AMOUNT[2]));  // open: en
  u_REV_2 REV_2 (.INPUT(multiplexer_2_out), .OUTPUT(REV_2_output));
  u_REV_3 REV_3 (.INPUT(multiplexer_3_out), .OUTPUT(REV_3_output));
  Multiplexer #(.width(32)) multiplexer_4 (
    .in0(multiplexer_3_out), .in1(REV_3_output), .out(multiplexer_4_out), .sel(REVERSE_AMOUNT[3]));  // open: en
  u_REV_4 REV_4 (.INPUT(multiplexer_4_out), .OUTPUT(REV_4_output));
  Multiplexer #(.width(32)) multiplexer_5 (
    .in0(multiplexer_4_out), .in1(REV_4_output), .out(OUTPUT), .sel(REVERSE_AMOUNT[4]));  // open: en
endmodule

module u_REV_0 (
  input  [31:0] INPUT,
  output [31:0] OUTPUT
);


  assign OUTPUT = {INPUT[30], INPUT[31], INPUT[28], INPUT[29], INPUT[26], INPUT[27], INPUT[24], INPUT[25], INPUT[22], INPUT[23], INPUT[20], INPUT[21], INPUT[18], INPUT[19], INPUT[16], INPUT[17], INPUT[14], INPUT[15], INPUT[12], INPUT[13], INPUT[10], INPUT[11], INPUT[8], INPUT[9], INPUT[6], INPUT[7], INPUT[4], INPUT[5], INPUT[2], INPUT[3], INPUT[0], INPUT[1]};
endmodule

module u_REV_1 (
  input  [31:0] INPUT,
  output [31:0] OUTPUT
);


  assign OUTPUT = {INPUT[29:28], INPUT[31:30], INPUT[25:24], INPUT[27:26], INPUT[21:20], INPUT[23:22], INPUT[17:16], INPUT[19:18], INPUT[13:12], INPUT[15:14], INPUT[9:8], INPUT[11:10], INPUT[5:4], INPUT[7:6], INPUT[1:0], INPUT[3:2]};
endmodule

module u_REV_2 (
  input  [31:0] INPUT,
  output [31:0] OUTPUT
);


  assign OUTPUT = {INPUT[27:24], INPUT[31:28], INPUT[19:16], INPUT[23:20], INPUT[11:8], INPUT[15:12], INPUT[3:0], INPUT[7:4]};
endmodule

module u_REV_3 (
  input  [31:0] INPUT,
  output [31:0] OUTPUT
);


  assign OUTPUT = {INPUT[23:16], INPUT[31:24], INPUT[7:0], INPUT[15:8]};
endmodule

module u_REV_4 (
  input  [31:0] INPUT,
  output [31:0] OUTPUT
);


  assign OUTPUT = {INPUT[15:0], INPUT[31:16]};
endmodule

// DIV
module u_DIV (
  input  [31:0] RS,
  input  [31:0] RI_IMM,
  output [31:0] OUTPUT
);

  wire comparator_1_eq, comparator_2_gt, comparator_2_lt, xor_1_out;
  wire [31:0] divider_1_out, FLIPSIGN_output, multiplexer_1_out, multiplexer_2_out, multiplexer_3_out,
       or_1_out, u_abs_1_output, u_abs_2_output;

  u_ABS u_abs_1 (.INPUT(RS), .OUTPUT(u_abs_1_output));
  u_ABS u_abs_2 (.INPUT(RI_IMM), .OUTPUT(u_abs_2_output));
  Comparator #(.width(32)) comparator_1 (.a(RI_IMM), .b({32{1'b0}}), .eq(comparator_1_eq));  // open: gt, lt
  Comparator #(.width(32)) comparator_2 (
    .a(RS), .b({32{1'b0}}), .gt(comparator_2_gt), .lt(comparator_2_lt));  // open: eq
  Divider #(.width(32)) divider_1 (.a(u_abs_1_output), .b(u_abs_2_output), .out(divider_1_out));  // open: upper, rem
  u_FLIPSIGN FLIPSIGN (.INPUT(divider_1_out), .OUTPUT(FLIPSIGN_output));
  xor xor_1 (xor_1_out, RS[31], RI_IMM[31]);
  Multiplexer #(.width(32)) multiplexer_1 (
    .in0({32{1'b0}}), .in1(32'h7fffffff), .out(multiplexer_1_out), .sel(comparator_2_gt));  // open: en
  assign or_1_out = multiplexer_1_out | {32{1'b0}} | multiplexer_2_out;  // OR_Gate or_1, 32 bits wide
  Multiplexer #(.width(32)) multiplexer_2 (
    .in0({32{1'b0}}), .in1(32'h80000000), .out(multiplexer_2_out), .sel(comparator_2_lt));  // open: en
  Multiplexer #(.width(32)) multiplexer_3 (
    .in0(divider_1_out), .in1(FLIPSIGN_output), .out(multiplexer_3_out), .sel(xor_1_out));  // open: en
  Multiplexer #(.width(32)) multiplexer_4 (
    .in0(multiplexer_3_out), .in1(or_1_out), .out(OUTPUT), .sel(comparator_1_eq));  // open: en

  // Other names for the same wires on the sheet: RI_IMM_SIGN = RI_IMM[31]; RS_SIGN = RS[31]
endmodule

// ABS
module u_ABS (
  input  [31:0] INPUT,
  output [31:0] OUTPUT
);

  wire [31:0] FLIPSIGN_output;

  Multiplexer #(.width(32)) multiplexer_1 (
    .in0(INPUT), .in1(FLIPSIGN_output), .out(OUTPUT), .sel(INPUT[31]));  // open: en
  u_FLIPSIGN FLIPSIGN (.INPUT(INPUT), .OUTPUT(FLIPSIGN_output));

  // Other names for the same wires on the sheet: RS_SIGN = INPUT[31]
endmodule

module u_FLIPSIGN (
  input  [31:0] INPUT,
  output [31:0] OUTPUT
);

  wire [31:0] not_1_out;

  assign not_1_out = ~INPUT;  // NOT_Gate not_1, 32 bits wide
  Adder #(.width(32)) adder_1 (.a(not_1_out), .b(32'h1), .out(OUTPUT));  // open: cin, cout
endmodule

// CTRL
module u_CTRL (
  input  [3:0] OP,
  input  [2:0] JC,
  input  [31:0] JC_VALUE,
  output J_SELECT,
  output JAL,
  output RD_WRITING_ENABLE,
  output WORD_MODE,
  output GO_MEM,
  output MEM_WRITE
);

  wire comparator_8_eq, J_TYPE, JC_0, JC_0_t, JC_0_t_t, multiplexer_1_out, not_1_out, OP_9, OP_11, OP_11_t,
       OP_11_t_t, OP_12, OP_13, OP_14, OP_14_t, or_1_out, or_2_out;

  Comparator #(.width(4)) comparator_1 (.a(OP), .b(4'b1111), .eq(J_TYPE));  // open: gt, lt
  Comparator #(.width(32)) comparator_2 (.a(JC_VALUE), .b({32{1'b0}}), .gt(JC_0_t_t), .eq(JC_0_t), .lt(JC_0));
  Comparator #(.width(4), .mode("unsigned")) comparator_3 (.a(OP), .b(4'b1001), .gt(OP_9));  // open: eq, lt
  Comparator #(.width(4), .mode("unsigned")) comparator_4 (
    .a(OP), .b(4'b1011), .gt(OP_11_t_t), .eq(OP_11_t), .lt(OP_11));
  Comparator #(.width(4), .mode("unsigned")) comparator_5 (.a(OP), .b(4'b1100), .eq(OP_12));  // open: gt, lt
  Comparator #(.width(4), .mode("unsigned")) comparator_6 (.a(OP), .b(4'b1101), .eq(OP_13));  // open: gt, lt
  Comparator #(.width(4), .mode("unsigned")) comparator_7 (.a(OP), .b(4'b1110), .eq(OP_14_t), .lt(OP_14));  // open: gt
  or or_1 (or_1_out, JC_0_t, JC_0);
  not not_1 (not_1_out, JC_0_t);
  or or_2 (or_2_out, JC_0_t_t, JC_0_t);
  Multiplexer #(.select(3)) multiplexer_1 (
    .in0(1'b1), .in1(JC_0_t_t), .in2(JC_0_t), .in3(JC_0), .in4(or_1_out), .in5(not_1_out), .in6(or_2_out),
    .in7(1'b1), .out(multiplexer_1_out), .sel(JC));  // open: en
  Comparator #(.width(3)) comparator_8 (.a(JC), .b(3'b111), .eq(comparator_8_eq));  // open: gt, lt
  and and_1 (J_SELECT, multiplexer_1_out, J_TYPE);
  and and_2 (JAL, J_TYPE, comparator_8_eq);
  or or_3 (RD_WRITING_ENABLE, JAL, OP_11, OP_12, OP_14_t);
  and and_3 (WORD_MODE, OP_11_t_t, OP_14);
  and and_4 (GO_MEM, OP_14, OP_9);
  or or_4 (MEM_WRITE, OP_11_t, OP_13);
endmodule

// DECODE
module u_DECODE (
  input  [31:0] Instruction,
  output [4:0] RD,
  output [4:0] RS,
  output [16:0] IMM,
  output [4:0] RI,
  output [23:0] ADDR,
  output [2:0] JC,
  output I,
  output [3:0] OP
);


  assign ADDR = Instruction[23:0];
  assign I = Instruction[27];
  assign IMM = Instruction[16:0];
  assign JC = Instruction[26:24];
  assign OP = Instruction[31:28];
  assign RD = Instruction[26:22];
  assign RI = Instruction[4:0];
  assign RS = Instruction[21:17];
endmodule

// PC
module u_PC (
  input  [23:0] PC_1,
  input  [23:0] J_ADDR,
  input  PC_SELECT,
  input  CLK,
  output [23:0] ADDR_1,
  output [23:0] ADDR
);

  wire [23:0] multiplexer_1_out;

  Multiplexer #(.width(24)) multiplexer_1 (
    .in0(PC_1), .in1(J_ADDR), .out(multiplexer_1_out), .sel(PC_SELECT));  // open: en
  Register #(.width(24)) register_1 (.D(multiplexer_1_out), .Q(ADDR), .clk(CLK));  // open: en, clr
  Adder #(.width(24)) adder_1 (.a(24'h1), .b(ADDR), .out(ADDR_1));  // open: cin, cout
endmodule

module u_SL (
  input  [31:0] RS,
  input  [4:0] RI_MM_0_4,
  output [31:0] SL_OUTPUT
);

  wire [4:0] subtractor_1_out;
  wire [31:0] multiplexer_1_out, shifter_1_out, shifter_2_out;

  Multiplexer #(.width(32)) multiplexer_1 (
    .in0({32{1'b0}}), .in1({32{1'b1}}), .out(multiplexer_1_out), .sel(RS[0]));  // open: en
  Subtractor #(.width(5)) subtractor_1 (.a({5{1'b1}}), .b(RI_MM_0_4), .out(subtractor_1_out));  // open: bin, bout
  Shifter #(.width(32)) shifter_1 (.in(RS), .\dist (RI_MM_0_4), .out(shifter_1_out));
  Shifter #(.width(32), .shift("lr")) shifter_2 (
    .in(multiplexer_1_out), .\dist (subtractor_1_out), .out(shifter_2_out));
  assign SL_OUTPUT = shifter_1_out | shifter_2_out;  // OR_Gate or_1, 32 bits wide

  // Other names for the same wires on the sheet: RI_IMM_0_4[4:0] = RI_MM_0_4; _0_bit = RS[0]
endmodule
